// Logisim project letters7segment.circ as structural Verilog
module main (
  input  [2:0] in_1
);

  wire [6:0] letters7seg_1_seg;

  _7_Segment_Display u_7_segment_display_1 (
    .g(letters7seg_1_seg[0]), .f(letters7seg_1_seg[1]), .a(letters7seg_1_seg[6]), .b(letters7seg_1_seg[5]),
    .e(letters7seg_1_seg[2]), .d(letters7seg_1_seg[3]), .c(letters7seg_1_seg[4]));  // open: dp
  letters7seg letters7seg_1 (.code(in_1), .seg(letters7seg_1_seg));
endmodule

// VHDL entity letters7seg, as the project stores it:
library ieee;
use ieee.std_logic_1164.all;

-- seg(6 downto 0) = a,b,c,d,e,f,g; 1 means ON (common cathode).
-- code 000=a, 001=b, 010=c, 011=d, 100=f, 101=g.
entity letters7seg is
    port (code : in std_logic_vector(2 downto 0);
          seg : out std_logic_vector(6 downto 0));
end letters7seg;

architecture rtl of letters7seg is
begin
    with code select
        seg <= "1110111" when "000", -- a (A)
               "0011111" when "001", -- b
               "1001110" when "010", -- c
               "0111101" when "011", -- d
               "1000111" when "100", -- f (F)
               "1011111" when "101", -- g (G-like)
               "0000000" when others;
end rtl;
