// Logisim project logic4led.circ as structural Verilog
module main (
  input  in_1,
  input  in_2,
  input  in_3,
  input  in_4
);

  wire logic4_1_out1, logic4_1_out2;

  LED led_1 (.in(logic4_1_out1));
  logic4 logic4_1 (.a(in_1), .b(in_2), .c(in_3), .d(in_4), .out1(logic4_1_out1), .out2(logic4_1_out2));
  LED led_2 (.in(logic4_1_out2));
endmodule

// VHDL entity logic4, as the project stores it:
library ieee;
use ieee.std_logic_1164.all;

entity logic4 is
    port (a, b, c, d : in std_logic;
          out1, out2 : out std_logic);
end logic4;

architecture rtl of logic4 is
begin
    out1 <= a and b and c and d;
    out2 <= a or b or c or d;
end rtl;
