// Logisim project mux8code.circ as structural Verilog
module main (
  input  [7:0] in_1,
  input  [2:0] in_2
);

  wire mux8_1_data_out;

  LED led_1 (.in(mux8_1_data_out));
  mux8 mux8_1 (.data_in(in_1), .sel(in_2), .data_out(mux8_1_data_out));
endmodule

// VHDL entity mux8, as the project stores it:
library ieee;
use ieee.std_logic_1164.all;

entity mux8 is
    port (data_in : in std_logic_vector(7 downto 0);
          sel : in std_logic_vector(2 downto 0);
          data_out : out std_logic);
end mux8;

architecture rtl of mux8 is
begin
    with sel select
        data_out <= data_in(0) when "000",
                    data_in(1) when "001",
                    data_in(2) when "010",
                    data_in(3) when "011",
                    data_in(4) when "100",
                    data_in(5) when "101",
                    data_in(6) when "110",
                    data_in(7) when others;
end rtl;
