// Logisim project vote.circ as structural Verilog
module main (
  input  [24:0] in_1
);

  wire vote25_1_result;

  LED led_1 (.in(vote25_1_result));
  vote25 vote25_1 (.vt(in_1), .result(vote25_1_result));
endmodule

// VHDL entity vote25, as the project stores it:
library ieee;
use ieee.std_logic_1164.all;

entity vote25 is
    port (vt : in std_logic_vector(24 downto 0);
          result : out std_logic);
end vote25;

architecture rtl of vote25 is
begin
    process(vt)
        variable votes : integer range 0 to 25;
    begin
        votes := 0;
        for i in vt'range loop
            if vt(i) = '1' then
                votes := votes + 1;
            end if;
        end loop;
        if votes >= 13 then
            result <= '1';
        else
            result <= '0';
        end if;
    end process;
end rtl;
