// Logisim project d_ff_async_gate.circ as structural Verilog: 1 circuit, main circuit main
module main (
  input  D,
  input  clk,
  input  set,
  input  clr,
  output Q,
  output nQ
);

  wire and_1_out, and_2_out, and_3_out, and_4_out, and_5_out, nand_1_p3, nand_2_p3, nand_3_p3, nand_4_p3,
       nand_5_p3, nand_6_p2, nand_6_p3, nand_8_p3, nand_9_p3, nand_10_p3, not_1_out, or_1_out, or_2_out,
       or_3_out, or_4_out;

  not not_1 (not_1_out, clk);
  // NAND_Gate nand_1: pin names not known; wires that end beside it: set, set, nand_1_p3
  // NAND_Gate nand_2: pin names not known; wires that end beside it: clr, clr, nand_2_p3
  and and_1 (and_1_out, set, nand_2_p3);
  // NAND_Gate nand_3: pin names not known; wires that end beside it: D, D, nand_3_p3
  // NAND_Gate nand_4: pin names not known; wires that end beside it: D, not_1_out, nand_4_p3
  // NAND_Gate nand_5: pin names not known; wires that end beside it: nand_3_p3, not_1_out, nand_5_p3
  and and_2 (and_2_out, nand_1_p3, nand_4_p3);
  and and_3 (and_3_out, nand_2_p3, nand_5_p3);
  or or_1 (or_1_out, clr, and_2_out);
  or or_2 (or_2_out, and_1_out, and_3_out);
  // NAND_Gate nand_6: pin names not known; wires that end beside it: or_1_out, nand_6_p2, nand_6_p3
  // NAND_Gate nand_7: pin names not known; wires that end beside it: or_2_out, nand_6_p3, nand_6_p2
  // NAND_Gate nand_8: pin names not known; wires that end beside it: nand_6_p3, nand_6_p3, nand_8_p3
  // NAND_Gate nand_9: pin names not known; wires that end beside it: nand_6_p3, clk, nand_9_p3
  // NAND_Gate nand_10: pin names not known; wires that end beside it: nand_8_p3, clk, nand_10_p3
  and and_4 (and_4_out, nand_1_p3, nand_9_p3);
  and and_5 (and_5_out, nand_2_p3, nand_10_p3);
  or or_3 (or_3_out, clr, and_4_out);
  or or_4 (or_4_out, and_1_out, and_5_out);
  // NAND_Gate nand_11: pin names not known; wires that end beside it: or_3_out, nQ, Q
  // NAND_Gate nand_12: pin names not known; wires that end beside it: or_4_out, Q, nQ

  // Notes on the sheet:
  //   clr: initial=0x1
  //   ASYNCHRONOUS SET / CLEAR D FF  |  priority: clr > set  |  rising edge
endmodule
