// Logisim project d_flipflop_gate.circ as structural Verilog: 1 circuit, main circuit main
module main (
  input  D,
  input  clk,
  output Q,
  output nQ
);

  wire nand_1_p3, nand_2_p3, nand_3_p3, nand_4_p2, nand_4_p3, nand_6_p3, nand_7_p3, nand_8_p3, not_1_out;

  not not_1 (not_1_out, clk);
  // NAND_Gate nand_1: pin names not known; wires that end beside it: D, D, nand_1_p3
  // NAND_Gate nand_2: pin names not known; wires that end beside it: D, not_1_out, nand_2_p3
  // NAND_Gate nand_3: pin names not known; wires that end beside it: nand_1_p3, not_1_out, nand_3_p3
  // NAND_Gate nand_4: pin names not known; wires that end beside it: nand_2_p3, nand_4_p2, nand_4_p3
  // NAND_Gate nand_5: pin names not known; wires that end beside it: nand_3_p3, nand_4_p3, nand_4_p2
  // NAND_Gate nand_6: pin names not known; wires that end beside it: nand_4_p3, nand_4_p3, nand_6_p3
  // NAND_Gate nand_7: pin names not known; wires that end beside it: nand_4_p3, clk, nand_7_p3
  // NAND_Gate nand_8: pin names not known; wires that end beside it: nand_6_p3, clk, nand_8_p3
  // NAND_Gate nand_9: pin names not known; wires that end beside it: nand_7_p3, nQ, Q
  // NAND_Gate nand_10: pin names not known; wires that end beside it: nand_8_p3, Q, nQ

  // Notes on the sheet:
  //   D FLIP-FLOP  |  NAND Master-Slave + NOT  |  positive edge
endmodule
