// Logisim project d_latch_gate.circ as structural Verilog: 1 circuit, main circuit main
module main (
  input  D,
  input  en,
  output Q,
  output nQ
);

  wire nand_1_p3, nand_2_p3, nand_3_p3;

  // NAND_Gate nand_1: pin names not known; wires that end beside it: D, D, nand_1_p3
  // NAND_Gate nand_2: pin names not known; wires that end beside it: D, en, nand_2_p3
  // NAND_Gate nand_3: pin names not known; wires that end beside it: nand_1_p3, en, nand_3_p3
  // NAND_Gate nand_4: pin names not known; wires that end beside it: nand_2_p3, nQ, Q
  // NAND_Gate nand_5: pin names not known; wires that end beside it: nand_3_p3, Q, nQ

  // Notes on the sheet:
  //   en: initial=0x1
  //   D LATCH  |  five NAND gates  |  en=1 transparent
endmodule
