// Logisim project jk_flipflop_gate.circ as structural Verilog: 1 circuit, main circuit main
module main (
  input  J,
  input  K,
  input  clk,
  output Q,
  output nQ
);

  wire nand_1_p3, nand_2_p3, nand_3_p3, nand_4_p3, nand_5_p3, nand_6_p3, nand_7_p3, nand_8_p2, nand_8_p3,
       nand_10_p3, nand_11_p3, nand_12_p3, not_1_out;

  // NAND_Gate nand_1: pin names not known; wires that end beside it: K, K, nand_1_p3
  // NAND_Gate nand_2: pin names not known; wires that end beside it: J, nQ, nand_2_p3
  // NAND_Gate nand_3: pin names not known; wires that end beside it: nand_1_p3, Q, nand_3_p3
  // NAND_Gate nand_4: pin names not known; wires that end beside it: nand_2_p3, nand_3_p3, nand_4_p3
  not not_1 (not_1_out, clk);
  // NAND_Gate nand_5: pin names not known; wires that end beside it: nand_4_p3, nand_4_p3, nand_5_p3
  // NAND_Gate nand_6: pin names not known; wires that end beside it: nand_4_p3, not_1_out, nand_6_p3
  // NAND_Gate nand_7: pin names not known; wires that end beside it: nand_5_p3, not_1_out, nand_7_p3
  // NAND_Gate nand_8: pin names not known; wires that end beside it: nand_6_p3, nand_8_p2, nand_8_p3
  // NAND_Gate nand_9: pin names not known; wires that end beside it: nand_7_p3, nand_8_p3, nand_8_p2
  // NAND_Gate nand_10: pin names not known; wires that end beside it: nand_8_p3, nand_8_p3, nand_10_p3
  // NAND_Gate nand_11: pin names not known; wires that end beside it: nand_8_p3, clk, nand_11_p3
  // NAND_Gate nand_12: pin names not known; wires that end beside it: nand_10_p3, clk, nand_12_p3
  // NAND_Gate nand_13: pin names not known; wires that end beside it: nand_11_p3, nQ, Q
  // NAND_Gate nand_14: pin names not known; wires that end beside it: nand_12_p3, Q, nQ

  // Notes on the sheet:
  //   K: initial=0x1
  //   JK FLIP-FLOP  |  NAND feedback + gate-built D FF  |  rising edge
endmodule
