// Logisim project rs_latch_gate.circ as structural Verilog: 1 circuit, main circuit main
module main (
  input  R,
  input  S,
  output Q,
  output nQ
);

  // NOR_Gate nor_1: pin names not known; wires that end beside it: R, nQ, Q
  // NOR_Gate nor_2: pin names not known; wires that end beside it: S, Q, nQ

  // Notes on the sheet:
  //   R: initial=0x1
  //   RS LATCH  |  NOR x2  |  S=1 Set, R=1 Reset
endmodule
